# Fritzing sketch bmw_remote_start (saved by Fritzing 0.9.3b)
perfboards: 1

parts:
  Componente1 = Arduino Nano (Rev3.0)
  M1 = RioRand LM2596  # not connected
  M2 = Niren can bus module [package=THT]
  U1 = Optocoupler [package=THT]
  U2 = Optocoupler [package=THT]
  U3 = Optocoupler [package=THT]
  R1 = Resistor [tolerance=±5% resistance=220 package=THT]
  R2 = Resistor [tolerance=±5% resistance=220 package=THT]
  R3 = Resistor [tolerance=±5% resistance=220 package=THT]

nets:
  N1: Componente1.GND, M2.pin2
  N2: Componente1.D2, R3.Pin_0
  N3: Componente1.D3, R2.Pin_0
  N4: Componente1.D4, R1.Pin_0
  N5: Componente1.D9, M2.pin3
  N6: Componente1.D10, M2.pin5
  N7: Componente1.D11/MOSI, M2.pin4
  N8: Componente1.D12/MISO, M2.pin6
  N9: Componente1.5V, M2.pin1
  N10: M2.pin10, M2.pin12
  N11: M2.pin11, M2.pin13
  N12: U1.Pin_1, R3.Pin_1
  N13: U2.Pin_1, R2.Pin_1
  N14: U3.Pin_1, R1.Pin_1

custom parts:
  Niren can bus module: Niren can bus module availabe on ebay and others. Pcb view assumes that you unsolder the 7 pin header and resolder it on the bottom of the module to connect to the pcb. The two jumpers and the can bus connector remain on the top of the board and don't appear in pcb view.
